// Logisim project Ekran.circ as structural Verilog: 1 circuit, main circuit main
module main (
  input  [3:0] in_1,
  input  [3:0] in_2,
  input  [3:0] in_3,
  input  in_4
);

  wire clock_1_out, counter_1_carry, keyboard_1_avail, main_2_p2, main_2_p4, not_1_out, register_1_q;
  wire [4:0] main_1_out_2, main_1_out_3, main_2_p3;
  wire [6:0] keyboard_1_data;
  wire [19:0] main_3_p4, main_3_p5, main_3_p6, main_3_p7, main_3_p8, main_3_p9, main_3_p10, main_3_p11,
       main_3_p12, main_3_p13, main_3_p14, main_3_p15, main_3_p16, main_3_p17, main_3_p18, main_3_p19,
       main_3_p20, main_3_p21, main_3_p22, main_3_p23, main_4_out_41, main_4_out_42, main_4_out_43,
       main_4_out_44, main_4_out_45, main_4_out_46, main_4_out_47, main_4_out_48, main_4_out_49,
       main_4_out_50, main_4_out_51, main_4_out_52, main_4_out_53, main_4_out_54, main_4_out_55,
       main_4_out_56, main_4_out_57, main_4_out_58, main_4_out_59, main_4_out_60, main_5_outy0,
       main_5_outy0_2, main_5_outy0_3, main_5_outy0_4, main_5_outy0_5, main_5_outy0_6, main_5_outy0_7,
       main_5_outy0_8, main_5_outy0_9, main_5_outy0_10, main_5_outy0_11, main_5_outy0_12, main_5_outy0_13,
       main_5_outy0_14, main_5_outy0_15, main_5_outy0_16, main_5_outy0_17, main_5_outy0_18, main_5_outy18,
       main_5_outy19, shifter_1_out, shifter_2_out, shifter_3_out;

  Keyboard keyboard_1 (
    .re(1'b1), .clr(keyboard_1_avail), .avail(keyboard_1_avail), .data(keyboard_1_data));  // open: clk
  Clock clock_1 (.out(clock_1_out));
  Counter #(.max('h64)) counter_1 (.carry(counter_1_carry), .clk(clock_1_out));  // open: load, D, count, Q, clr
  LR_main main_1 (.in_1(keyboard_1_data), .out_2(main_1_out_2), .out_3(main_1_out_3));
  // Enter_Up_Down_main main_2: pin names not known; wires that end beside it: keyboard_1_data, main_2_p2, main_2_p3, main_2_p4
  Counter counter_2 (.clk(counter_1_carry));  // open: load, D, count, Q, carry, clr
  not not_1 (not_1_out, in_4);
  Shifter #(.width(20)) shifter_1 (.in(20'h200), .\dist (main_1_out_2), .out(shifter_1_out));
  Register #(.width(1), .trigger("high")) register_1 (
    .D(clock_1_out), .Q(register_1_q), .clk(not_1_out), .clr(in_4));  // open: en
  Shifter #(.width(20), .shift("lr")) shifter_2 (.in(shifter_1_out), .\dist (main_1_out_3), .out(shifter_2_out));
  Shifter #(.width(20), .shift("lr")) shifter_3 (.in(20'h80000), .\dist (main_2_p3), .out(shifter_3_out));
  // Uu_Down32_main main_3: pin names not known; wires that end beside it: main_2_p3, shifter_2_out, register_1_q, main_3_p4, main_3_p5, main_3_p6, main_3_p7, main_3_p8, main_3_p9, main_3_p10, main_3_p11, main_3_p12, main_3_p13, main_3_p14, main_3_p15, main_3_p16, main_3_p17, main_3_p18, main_3_p19, main_3_p20, main_3_p21, main_3_p22, main_3_p23
  Register32x32_main main_4 (
    .in_1(main_3_p4), .in_2(main_3_p5), .in_3(main_3_p6), .in_4(main_3_p7), .in_5(main_3_p8),
    .in_6(main_3_p9), .in_7(main_3_p10), .in_8(main_3_p11), .in_9(main_3_p12), .in_10(main_3_p13),
    .in_11(main_3_p14), .in_12(main_3_p15), .in_13(main_3_p16), .in_14(main_3_p17), .in_15(main_3_p18),
    .in_16(main_3_p19), .in_17(main_3_p20), .in_18(main_3_p21), .in_19(main_3_p22), .in_20(main_3_p23),
    .out_41(main_4_out_41), .out_42(main_4_out_42), .out_43(main_4_out_43), .out_44(main_4_out_44),
    .out_45(main_4_out_45), .out_46(main_4_out_46), .out_47(main_4_out_47), .out_48(main_4_out_48),
    .out_49(main_4_out_49), .out_50(main_4_out_50), .out_51(main_4_out_51), .out_52(main_4_out_52),
    .out_53(main_4_out_53), .out_54(main_4_out_54), .out_55(main_4_out_55), .out_56(main_4_out_56),
    .out_57(main_4_out_57), .out_58(main_4_out_58), .out_59(main_4_out_59), .out_60(main_4_out_60),
    .in_21(main_5_outy0), .in_22(main_5_outy0_2), .in_23(main_5_outy0_3), .in_24(main_5_outy0_4),
    .in_25(main_5_outy0_5), .in_26(main_5_outy0_6), .in_27(main_5_outy0_7), .in_28(main_5_outy0_8),
    .in_29(main_5_outy0_9), .in_30(main_5_outy0_10), .in_31(main_5_outy0_11), .in_32(main_5_outy0_12),
    .in_33(main_5_outy0_13), .in_34(main_5_outy0_14), .in_35(main_5_outy0_15), .in_36(main_5_outy0_16),
    .in_37(main_5_outy0_17), .in_38(main_5_outy0_18), .in_39(main_5_outy18), .in_40(main_5_outy19));
  DotMatrix #(.inputtype("row"), .matrixcols(20), .matrixrows(20)) dotmatrix_1 (
    .row0(main_4_out_41), .row1(main_4_out_42), .row2(main_4_out_43), .row3(main_4_out_44),
    .row4(main_4_out_45), .row5(main_4_out_46), .row6(main_4_out_47), .row7(main_4_out_48),
    .row8(main_4_out_49), .row9(main_4_out_50), .row10(main_4_out_51), .row11(main_4_out_52),
    .row12(main_4_out_53), .row13(main_4_out_54), .row14(main_4_out_55), .row15(main_4_out_56),
    .row16(main_4_out_57), .row17(main_4_out_58), .row18(main_4_out_59), .row19(main_4_out_60));
  Modol_Obliczeniowy_20x20_main main_5 (
    .if_x_in_die(in_1), .if_x_n_born(in_2), .if_x_in_die_2(in_3), .Reset(main_2_p4), .CLK(counter_1_carry),
    .CLK_Enabler(in_4), .Overwrite(main_2_p2), .X(shifter_2_out), .Y(shifter_3_out), .OutY0(main_5_outy0),
    .OutY0_2(main_5_outy0_2), .OutY0_3(main_5_outy0_3), .OutY0_4(main_5_outy0_4), .OutY0_5(main_5_outy0_5),
    .OutY0_6(main_5_outy0_6), .OutY0_7(main_5_outy0_7), .OutY0_8(main_5_outy0_8), .OutY0_9(main_5_outy0_9),
    .OutY0_10(main_5_outy0_10), .OutY0_11(main_5_outy0_11), .OutY0_12(main_5_outy0_12),
    .OutY0_13(main_5_outy0_13), .OutY0_14(main_5_outy0_14), .OutY0_15(main_5_outy0_15),
    .OutY0_16(main_5_outy0_16), .OutY0_17(main_5_outy0_17), .OutY0_18(main_5_outy0_18),
    .OutY18(main_5_outy18), .OutY19(main_5_outy19));
endmodule
