// Logisim project Register1x32.circ as structural Verilog: 1 circuit, main circuit main
module main (
  input  [31:0] in_1,
  input  in_2,
  input  in_3,
  output [31:0] out_4
);

  wire [31:0] register_1_q;

  Register #(.width(32)) register_1 (.D(out_4), .Q(register_1_q), .clk(in_3), .clr(in_2));  // open: en
  Adder #(.width(32)) adder_1 (.a(in_1), .b(register_1_q), .out(out_4));  // open: cin, cout
endmodule
