// Logisim project Register32x32.circ as structural Verilog: 1 circuit, main circuit main
module main (
  input  [19:0] in_1,
  input  [19:0] in_2,
  input  [19:0] in_3,
  input  [19:0] in_4,
  input  [19:0] in_5,
  input  [19:0] in_6,
  input  [19:0] in_7,
  input  [19:0] in_8,
  input  [19:0] in_9,
  input  [19:0] in_10,
  input  [19:0] in_11,
  input  [19:0] in_12,
  input  [19:0] in_13,
  input  [19:0] in_14,
  input  [19:0] in_15,
  input  [19:0] in_16,
  input  [19:0] in_17,
  input  [19:0] in_18,
  input  [19:0] in_19,
  input  [19:0] in_20,
  input  [19:0] in_21,
  input  [19:0] in_22,
  input  [19:0] in_23,
  input  [19:0] in_24,
  input  [19:0] in_25,
  input  [19:0] in_26,
  input  [19:0] in_27,
  input  [19:0] in_28,
  input  [19:0] in_29,
  input  [19:0] in_30,
  input  [19:0] in_31,
  input  [19:0] in_32,
  input  [19:0] in_33,
  input  [19:0] in_34,
  input  [19:0] in_35,
  input  [19:0] in_36,
  input  [19:0] in_37,
  input  [19:0] in_38,
  input  [19:0] in_39,
  input  [19:0] in_40,
  output [19:0] out_41,
  output [19:0] out_42,
  output [19:0] out_43,
  output [19:0] out_44,
  output [19:0] out_45,
  output [19:0] out_46,
  output [19:0] out_47,
  output [19:0] out_48,
  output [19:0] out_49,
  output [19:0] out_50,
  output [19:0] out_51,
  output [19:0] out_52,
  output [19:0] out_53,
  output [19:0] out_54,
  output [19:0] out_55,
  output [19:0] out_56,
  output [19:0] out_57,
  output [19:0] out_58,
  output [19:0] out_59,
  output [19:0] out_60
);

  wire main_20_p3;

  Register1x32_main main_1 (.in_1(in_1), .in_2(in_21), .out_3(out_41));
  Register1x32_main main_2 (.in_1(in_2), .in_2(in_22), .out_3(out_42));
  Register1x32_main main_3 (.in_1(in_3), .in_2(in_23), .out_3(out_43));
  Register1x32_main main_4 (.in_1(in_4), .in_2(in_24), .out_3(out_44));
  Register1x32_main main_5 (.in_1(in_5), .in_2(in_25), .out_3(out_45));
  Register1x32_main main_6 (.in_1(in_6), .in_2(in_26), .out_3(out_46));
  Register1x32_main main_7 (.in_1(in_7), .in_2(in_27), .out_3(out_47));
  Register1x32_main main_8 (.in_1(in_8), .in_2(in_28), .out_3(out_48));
  Register1x32_main main_9 (.in_1(in_9), .in_2(in_29), .out_3(out_49));
  Register1x32_main main_10 (.in_1(in_10), .in_2(in_30), .out_3(out_50));
  Register1x32_main main_11 (.in_1(in_11), .in_2(in_31), .out_3(out_51));
  Register1x32_main main_12 (.in_1(in_12), .in_2(in_32), .out_3(out_52));
  Register1x32_main main_13 (.in_1(in_13), .in_2(in_33), .out_3(out_53));
  Register1x32_main main_14 (.in_1(in_14), .in_2(in_34), .out_3(out_54));
  Register1x32_main main_15 (.in_1(in_15), .in_2(in_35), .out_3(out_55));
  Register1x32_main main_16 (.in_1(in_16), .in_2(in_36), .out_3(out_56));
  Register1x32_main main_17 (.in_1(in_17), .in_2(in_37), .out_3(out_57));
  Register1x32_main main_18 (.in_1(in_18), .in_2(in_38), .out_3(out_58));
  Register1x32_main main_19 (.in_1(in_19), .in_2(in_39), .out_3(out_59));
  // Register1x32_main main_20: pin names not known; wires that end beside it: in_20, in_40, main_20_p3, out_60
endmodule
