// Logisim project Uu_Down1.circ as structural Verilog: 1 circuit, main circuit main
module main (
  input  [31:0] in_1,
  input  [4:0] in_2,
  input  [4:0] in_3,
  output [31:0] out_4
);

  wire comparator_1_eq, comparator_1_gt, comparator_1_lt, or_1_out;

  Comparator #(.width(5)) comparator_1 (
    .a(in_2), .b(in_3), .gt(comparator_1_gt), .eq(comparator_1_eq), .lt(comparator_1_lt));
  or or_1 (or_1_out, comparator_1_gt, comparator_1_lt);
  Register #(.width(32), .trigger("high")) register_1 (
    .D(in_1), .Q(out_4), .clk(comparator_1_eq), .clr(or_1_out));  // open: en
endmodule
