// Logisim project Uu_Down32.circ as structural Verilog: 1 circuit, main circuit main
module main (
  input  [4:0] in_1,
  input  [19:0] in_2,
  input  in_3,
  input  in_4,
  output [19:0] out_5,
  output [19:0] out_6,
  output [19:0] out_7,
  output [19:0] out_8,
  output [19:0] out_9,
  output [19:0] out_10,
  output [19:0] out_11,
  output [19:0] out_12,
  output [19:0] out_13,
  output [19:0] out_14,
  output [19:0] out_15,
  output [19:0] out_16,
  output [19:0] out_17,
  output [19:0] out_18,
  output [19:0] out_19,
  output [19:0] out_20,
  output [19:0] out_21,
  output [19:0] out_22,
  output [19:0] out_23,
  output [19:0] out_24
);

  Uu_Down1_main main_1 (.in_1(in_2), .in_2(in_1), .in_3(5'b10011), .in_4(in_3), .out_6(out_5), .in_5(in_4));
  Uu_Down1_main main_2 (.in_1(in_2), .in_2(in_1), .in_3(5'b10010), .in_4(in_3), .out_6(out_6), .in_5(in_4));
  Uu_Down1_main main_3 (.in_1(in_2), .in_2(in_1), .in_3(5'b10001), .in_4(in_3), .out_6(out_7), .in_5(in_4));
  Uu_Down1_main main_4 (.in_1(in_2), .in_2(in_1), .in_3(5'b10000), .in_4(in_3), .out_6(out_8), .in_5(in_4));
  Uu_Down1_main main_5 (.in_1(in_2), .in_2(in_1), .in_3(5'b01111), .in_4(in_3), .out_6(out_9), .in_5(in_4));
  Uu_Down1_main main_6 (.in_1(in_2), .in_2(in_1), .in_3(5'b01110), .in_4(in_3), .out_6(out_10), .in_5(in_4));
  Uu_Down1_main main_7 (.in_1(in_2), .in_2(in_1), .in_3(5'b01101), .in_4(in_3), .out_6(out_11), .in_5(in_4));
  Uu_Down1_main main_8 (.in_1(in_2), .in_2(in_1), .in_3(5'b01100), .in_4(in_3), .out_6(out_12), .in_5(in_4));
  Uu_Down1_main main_9 (.in_1(in_2), .in_2(in_1), .in_3(5'b01011), .in_4(in_3), .out_6(out_13), .in_5(in_4));
  Uu_Down1_main main_10 (.in_1(in_2), .in_2(in_1), .in_3(5'b01010), .in_4(in_3), .out_6(out_14), .in_5(in_4));
  Uu_Down1_main main_11 (.in_1(in_2), .in_2(in_1), .in_3(5'b01001), .in_4(in_3), .out_6(out_15), .in_5(in_4));
  Uu_Down1_main main_12 (.in_1(in_2), .in_2(in_1), .in_3(5'b01000), .in_4(in_3), .out_6(out_16), .in_5(in_4));
  Uu_Down1_main main_13 (.in_1(in_2), .in_2(in_1), .in_3(5'b00111), .in_4(in_3), .out_6(out_17), .in_5(in_4));
  Uu_Down1_main main_14 (.in_1(in_2), .in_2(in_1), .in_3(5'b00110), .in_4(in_3), .out_6(out_18), .in_5(in_4));
  Uu_Down1_main main_15 (.in_1(in_2), .in_2(in_1), .in_3(5'b00101), .in_4(in_3), .out_6(out_19), .in_5(in_4));
  Uu_Down1_main main_16 (.in_1(in_2), .in_2(in_1), .in_3(5'b00100), .in_4(in_3), .out_6(out_20), .in_5(in_4));
  Uu_Down1_main main_17 (.in_1(in_2), .in_2(in_1), .in_3(5'b00011), .in_4(in_3), .out_6(out_21), .in_5(in_4));
  Uu_Down1_main main_18 (.in_1(in_2), .in_2(in_1), .in_3(5'b00010), .in_4(in_3), .out_6(out_22), .in_5(in_4));
  Uu_Down1_main main_19 (.in_1(in_2), .in_2(in_1), .in_3(5'b00001), .in_4(in_3), .out_6(out_23), .in_5(in_4));
  Uu_Down1_main main_20 (.in_1(in_2), .in_2(in_1), .in_3({5{1'b0}}), .in_4(in_3), .out_6(out_24), .in_5(in_4));
endmodule
